# Fritzing sketch rx_tx (saved by Fritzing 1.0.5)

parts:
  Part1 = Arduino Nano (Rev3.0)
  Part2 = NRF24L01+ Breakout Board
  Part3 = Arduino Nano (Rev3.0)
  Part4 = NRF24L01+ Breakout Board
  U1 = RJ45 Jack [package=rj45-8]
  U2 = LIPO-110mAh [package=lipo-110]  # not connected
  U3 = RJ45 Jack [package=rj45-8]
  C2 = Electrolytic Capacitor [capacitance=6.8µF voltage=10V package="0807 [SMD, electrolytic]"]
  R1 = Resistor [tolerance=±5% resistance=4.7k package="1206 [SMD]"]
  C3 = Electrolytic Capacitor [capacitance=6.8µF voltage=10V package="0807 [SMD, electrolytic]"]
  C4 = Electrolytic Capacitor [capacitance=6.8µF voltage=10V package="0807 [SMD, electrolytic]"]
  R2 = Resistor [tolerance=±5% resistance=4.7k package="1206 [SMD]"]
  R3 = Resistor [tolerance=±5% resistance=4.7k package="1206 [SMD]"]

nets:
  GND: Part1.GND, Part2.GND, C3.-
  N1: Part1.D3, R3.Pin_0
  N2: Part1.D5, R2.Pin_0
  N3: Part1.D6, R1.Pin_0
  N4: Part1.D7, Part2.CE
  N5: Part1.D8, Part2.CS
  N6: Part1.D10, Part2.MISO
  N7: Part1.D11/MOSI, Part2.MOSI
  N8: Part1.D12/MISO, Part2.SCK
  3V3: Part1.3V3, Part2.VCC
  GND_2: Part3.GND, Part4.GND
  N9: Part3.D7, Part4.CE
  N10: Part3.D8, Part4.CS
  N11: Part3.D11/MOSI, Part4.MOSI
  N12: Part3.D12/MISO, Part4.SCK
  N13: Part3.A6, U1.5
  N14: Part3.A3, U1.6
  N15: Part3.A1, U1.7
  3V3_2: Part3.3V3, Part4.VCC, U1.8
  N16: U3.6, C4.+, R3.Pin_1
  N17: U3.7, C3.+, R2.Pin_1
  N18: U3.8, C2.+, R1.Pin_1
  N19: C2.-, C4.-

notes:
  I used 6.8µF
  (4-10µF should do the trick)
  TX: to pedals
  RX: to base
  R = 4.7kΩ
